// Logisim project cruce_semáforo_final.circ as structural Verilog: 1 circuit, main circuit main
module main (
  input  in_1,
  input  in_2
);

  wire and_1_out, and_2_out, and_3_out, and_4_out, and_5_out, and_6_out, and_7_out, and_8_out, and_9_out,
       and_10_out, and_11_out, and_12_out, and_13_out, and_14_out, and_15_out, and_16_out, and_17_out,
       and_18_out, and_19_out, and_20_out, and_21_out, and_22_out, and_23_out, and_24_out, and_25_out,
       and_26_out, and_27_out, and_28_out, and_29_out, and_30_out, and_31_out, and_32_out, and_33_out,
       and_34_out, button_1_out, button_2_out, clock_1_out, d_ff_1_q, d_ff_2_q, j_k_ff_1_q, j_k_ff_1_qn,
       j_k_ff_2_q, j_k_ff_2_qn, j_k_ff_3_q, j_k_ff_3_qn, j_k_ff_4_q, j_k_ff_4_qn, j_k_ff_5_q, not_1_out,
       not_2_out, not_3_out, not_4_out, not_5_out, or_1_out, or_2_out, or_3_out, or_4_out, or_5_out,
       or_6_out, or_7_out, or_8_out, P1_V_out, P2_V_out, S1_A_out, S1_R_out, S1_V_out, S2_A_out, S2_R_out,
       S2_V_out, undriven, undriven_2, undriven_3, undriven_4;

  or or_1 (or_1_out, and_34_out, and_33_out);
  or or_2 (or_2_out, and_34_out, and_33_out);
  or or_3 (or_3_out, and_34_out, and_33_out);
  or or_4 (or_4_out, and_34_out, and_33_out);
  Clock clock_1 (.out(clock_1_out));
  J_K_Flip_Flop j_k_ff_1 (
    .J(in_1), .clk(clock_1_out), .K(in_2), .Q(j_k_ff_1_q), .Qn(j_k_ff_1_qn), .preset(or_1_out),
    .reset(undriven_2));  // open: en
  J_K_Flip_Flop j_k_ff_2 (
    .J(in_1), .clk(j_k_ff_1_qn), .K(in_2), .Q(j_k_ff_2_q), .Qn(j_k_ff_2_qn), .preset(undriven),
    .reset(or_2_out));  // open: en
  not not_1 (not_1_out, j_k_ff_1_q);
  J_K_Flip_Flop j_k_ff_3 (
    .J(in_1), .clk(j_k_ff_2_qn), .K(in_2), .Q(j_k_ff_3_q), .Qn(j_k_ff_3_qn), .preset(undriven_3),
    .reset(or_4_out));  // open: en
  not not_2 (not_2_out, j_k_ff_2_q);
  J_K_Flip_Flop j_k_ff_4 (
    .J(in_1), .clk(j_k_ff_3_qn), .K(in_2), .Q(j_k_ff_4_q), .Qn(j_k_ff_4_qn), .preset(undriven_4),
    .reset(or_3_out));  // open: en
  not not_3 (not_3_out, j_k_ff_3_q);
  J_K_Flip_Flop j_k_ff_5 (
    .J(in_1), .clk(j_k_ff_4_qn), .K(in_2), .Q(j_k_ff_5_q), .preset(and_33_out), .reset(and_34_out));  // open: Qn, en
  not not_4 (not_4_out, j_k_ff_4_q);
  not not_5 (not_5_out, j_k_ff_5_q);
  and and_1 (and_1_out, not_1_out, not_2_out, not_3_out, not_4_out, not_5_out);
  and and_2 (and_2_out, not_5_out, not_4_out, not_3_out, not_2_out, j_k_ff_1_q);
  and and_3 (and_3_out, not_5_out, not_4_out, not_3_out, j_k_ff_2_q, not_1_out);
  and and_4 (and_4_out, not_5_out, not_4_out, not_3_out, j_k_ff_2_q, j_k_ff_1_q);
  and and_5 (and_5_out, not_5_out, not_4_out, j_k_ff_3_q, not_2_out, not_1_out);
  and and_6 (and_6_out, not_5_out, not_4_out, j_k_ff_3_q, not_2_out, j_k_ff_1_q);
  and and_7 (and_7_out, not_5_out, not_4_out, j_k_ff_3_q, j_k_ff_2_q, not_1_out);
  and and_8 (and_8_out, not_5_out, not_4_out, j_k_ff_3_q, j_k_ff_2_q, j_k_ff_1_q);
  and and_9 (and_9_out, not_5_out, j_k_ff_4_q, not_3_out, not_2_out, not_1_out);
  and and_10 (and_10_out, not_5_out, j_k_ff_4_q, not_3_out, not_2_out, j_k_ff_1_q);
  and and_11 (and_11_out, not_5_out, j_k_ff_4_q, not_3_out, j_k_ff_2_q, not_1_out);
  and and_12 (and_12_out, not_5_out, j_k_ff_4_q, not_3_out, j_k_ff_2_q, j_k_ff_1_q);
  and and_13 (and_13_out, not_5_out, j_k_ff_4_q, j_k_ff_3_q, not_2_out, not_1_out);
  and and_14 (and_14_out, not_5_out, j_k_ff_4_q, j_k_ff_3_q, not_2_out, j_k_ff_1_q);
  and and_15 (and_15_out, not_5_out, j_k_ff_4_q, j_k_ff_3_q, j_k_ff_2_q, not_1_out);
  and and_16 (and_16_out, not_5_out, j_k_ff_4_q, j_k_ff_3_q, j_k_ff_2_q, j_k_ff_1_q);
  and and_17 (and_17_out, j_k_ff_5_q, not_4_out, not_3_out, not_2_out, not_1_out);
  and and_18 (and_18_out, j_k_ff_5_q, not_4_out, not_3_out, not_2_out, j_k_ff_1_q);
  and and_19 (and_19_out, j_k_ff_5_q, not_4_out, not_3_out, j_k_ff_2_q, not_1_out);
  and and_20 (and_20_out, j_k_ff_5_q, not_4_out, not_3_out, j_k_ff_2_q, j_k_ff_1_q);
  and and_21 (and_21_out, j_k_ff_5_q, not_4_out, j_k_ff_3_q, not_2_out, not_1_out);
  and and_22 (and_22_out, j_k_ff_5_q, not_4_out, j_k_ff_3_q, not_2_out, j_k_ff_1_q);
  and and_23 (and_23_out, j_k_ff_5_q, not_4_out, j_k_ff_3_q, j_k_ff_2_q, not_1_out);
  and and_24 (and_24_out, j_k_ff_5_q, not_4_out, j_k_ff_3_q, j_k_ff_2_q, j_k_ff_1_q);
  and and_25 (and_25_out, j_k_ff_5_q, j_k_ff_4_q, not_3_out, not_2_out, not_1_out);
  and and_26 (and_26_out, j_k_ff_5_q, j_k_ff_4_q, not_3_out, not_2_out, j_k_ff_1_q);
  and and_27 (and_27_out, j_k_ff_5_q, j_k_ff_4_q, not_3_out, j_k_ff_2_q, not_1_out);
  and and_28 (and_28_out, j_k_ff_5_q, j_k_ff_4_q, not_3_out, j_k_ff_2_q, j_k_ff_1_q);
  and and_29 (and_29_out, j_k_ff_5_q, j_k_ff_4_q, j_k_ff_3_q, not_2_out, not_1_out);
  and and_30 (and_30_out, j_k_ff_5_q, j_k_ff_4_q, j_k_ff_3_q, not_2_out, j_k_ff_1_q);
  and and_31 (and_31_out, j_k_ff_5_q, j_k_ff_4_q, j_k_ff_3_q, j_k_ff_2_q, not_1_out);
  and and_32 (and_32_out, j_k_ff_5_q, j_k_ff_4_q, j_k_ff_3_q, j_k_ff_2_q, j_k_ff_1_q);
  or S1_V (S1_V_out, and_2_out, and_3_out, and_4_out, and_5_out, and_6_out, and_7_out, and_8_out, and_9_out, and_10_out, and_11_out, and_12_out, and_13_out, and_14_out);
  or S1_A (S1_A_out, and_15_out, and_16_out);
  or S1_R (S1_R_out, and_17_out, and_18_out, and_19_out, and_20_out, and_21_out, and_22_out, and_23_out, and_24_out, and_1_out, and_25_out, and_26_out, and_27_out, and_28_out, and_29_out, and_30_out, and_31_out, and_32_out);
  or P1_V (P1_V_out, and_18_out, and_19_out, and_20_out, and_21_out, and_22_out, and_23_out, and_24_out, and_25_out, and_26_out, and_28_out, and_30_out, and_32_out);
  or S2_V (S2_V_out, and_18_out, and_19_out, and_20_out, and_21_out, and_22_out, and_23_out, and_24_out, and_25_out, and_26_out, and_27_out, and_28_out, and_29_out, and_30_out);
  or S2_R (S2_R_out, and_1_out, and_2_out, and_3_out, and_4_out, and_5_out, and_6_out, and_7_out, and_8_out, and_9_out, and_10_out, and_11_out, and_12_out, and_13_out, and_14_out, and_15_out, and_16_out, and_17_out);
  or S2_A (S2_A_out, and_31_out, and_32_out);
  or P2_V (P2_V_out, and_2_out, and_3_out, and_4_out, and_5_out, and_6_out, and_7_out, and_8_out, and_9_out, and_10_out, and_12_out, and_14_out, and_16_out);
  or or_5 (or_5_out, and_26_out, and_27_out, and_28_out, and_29_out);
  or or_6 (or_6_out, and_10_out, and_11_out, and_12_out, and_13_out);
  or or_7 (or_7_out, S1_V_out, S1_A_out);
  or or_8 (or_8_out, S2_V_out, S2_A_out);
  D_Flip_Flop d_ff_1 (.clk(clock_1_out), .D(or_6_out), .Q(d_ff_1_q));  // open: Qn, preset, en, reset
  D_Flip_Flop d_ff_2 (.clk(clock_1_out), .D(or_5_out), .Q(d_ff_2_q));  // open: Qn, preset, en, reset
  LED led_1 (.in(or_8_out));
  LED led_2 (.in(P2_V_out));
  LED led_3 (.in(or_8_out));
  LED led_4 (.in(P2_V_out));
  LED led_5 (.in(or_7_out));
  LED led_6 (.in(P1_V_out));
  LED led_7 (.in(S2_R_out));
  LED led_8 (.in(S2_A_out));
  LED led_9 (.in(S2_V_out));
  LED led_10 (.in(or_7_out));
  LED led_11 (.in(P1_V_out));
  Button button_1 (.out(button_1_out));
  and and_33 (and_33_out, button_1_out, d_ff_2_q);
  LED led_12 (.in(S1_R_out));
  LED led_13 (.in(S1_A_out));
  LED led_14 (.in(S1_V_out));
  LED led_15 (.in(S1_R_out));
  LED led_16 (.in(S1_A_out));
  LED led_17 (.in(S1_V_out));
  LED led_18 (.in(or_7_out));
  LED led_19 (.in(P1_V_out));
  LED led_20 (.in(or_8_out));
  LED led_21 (.in(P2_V_out));
  LED led_22 (.in(S2_R_out));
  LED led_23 (.in(S2_A_out));
  LED led_24 (.in(S2_V_out));
  LED led_25 (.in(or_7_out));
  LED led_26 (.in(P1_V_out));
  LED led_27 (.in(or_8_out));
  LED led_28 (.in(P2_V_out));
  Button button_2 (.out(button_2_out));
  and and_34 (and_34_out, button_2_out, d_ff_1_q);

  // Notes on the sheet:
  //   P1
  //   P2
  //   SEMÁFORO #2 DESDE ACÁ
  //   S en A y V activa P en R
  //   S en A y V activa P en R
  //   V1 parpadeando
  //   P2
  //   P1
  //   S1
  //   BOTÓN PEATONAL1
  //   S1: Vertical
  //   S2: Horizontal
  //   Resetear semáforo a los que cruzan así:
  //   Se activa si P está V y parpadeando.
  //   CÓMO HACER PARA QUE
  //   SE RESETEE UNA SOLA VEZ??
  //   NO TENGO IDEA
  //   YA INTENTÉ USANDO LO QUE HEMOS VISTO, QUIZÁ METIENDO MANO A OTRAS
  //   COSAS
  //   BOTÓN PEATONAL2
endmodule
